# Fritzing sketch pn532 (saved by Fritzing 0.9.3b)

parts:
  Componente1 = RFID-RC522-v2
  Componente2 = Arduino Uno (Rev3)

nets:
  N1: Componente1.SCK, Componente2.D13/SCK
  N2: Componente1.MI, Componente2.D12/MISO
  N3: Componente1.MOSI, Componente2.D11_PWM/MOSI
  N4: Componente1.MISO, Componente2.D10_PWM/SS
  N5: Componente1.IRQ, Componente2.D3_PWM
  N6: Componente1.RST, Componente2.D2
  GND: Componente1.GND, Componente2.GND
  N7: Componente1.5_V, Componente2.5V

custom parts:
  RFID-RC522-v2: A simple China made RFID-RC522 Reader; do check the pin labels, as this is a MFRC522 based clone.
