# Fritzing sketch rc522 (saved by Fritzing 0.9.3b)

parts:
  Componente1 = Arduino Uno (Rev3)
  Componente2 = RFID-RC522-v2

nets:
  N1: Componente1.D9_PWM, Componente2.RST
  N2: Componente1.D10_PWM/SS, Componente2.SDA
  N3: Componente1.D11_PWM/MOSI, Componente2.MOSI
  N4: Componente1.D12/MISO, Componente2.MISO
  N5: Componente1.D13/SCK, Componente2.SCK
  5V: Componente1.5V, Componente2.3.3V
  GND: Componente1.GND, Componente2.GND

custom parts:
  RFID-RC522-v2: A simple China made RFID-RC522 Reader; do check the pin labels, as this is a MFRC522 based clone.
