# Fritzing sketch keylogger ps2 (saved by Fritzing 0.9.3b)
breadboards: 1

parts:
  Componente1 = Arduino Leonardo (Rev3b)
  Componente2 = MicroSD Card Module
  U2 = mini DIN 6 Connector [package=mini-din6]
  U1 = mini DIN 6 Connector [package=mini-din6]

nets:
  N1: Componente1.D2/SDA, U2.1, U1.1
  N2: Componente1.D3_PWM/SCL, U2.5, U1.5
  N3: Componente1.D4/A6, Componente2.CS
  3V3: Componente1.3V3, Componente2.VCC
  GND: Componente1.GND, Componente2.GND, U2.3, U1.3
  N4: U2.4, U1.4
